// Logisim project lab09part1-jlh238.circ as structural Verilog
module asdfad (
  input  asdf,
  input  asda
);
endmodule

module trop (
  input  tupac,
  input  wupac
);
endmodule

module question (
  input  A1,
  input  A0,
  input  B1,
  input  B0,
  input  Y
);
endmodule

module asdfasdf (
  input  A1,
  input  A0,
  input  B1,
  input  B0,
  output x,
  output zero,
  output one
);
endmodule

module dafasdf (
  input  A1,
  input  A0,
  input  B1,
  input  B0,
  output Y
);

  and and_1 (Y, 1'b1, 1'b0);
endmodule

module adf (
  input  A1,
  input  A0,
  input  B1,
  input  B0,
  output Y
);


  assign Y = 1'b1;
endmodule

module a (
  input  A1,
  input  A0,
  input  B1,
  input  B0,
  output Y
);

  and and_1 (Y, 1'b1, 1'b0);
endmodule

module lab09part1_jlh238 (
  input  A1,
  input  A0,
  input  B1,
  input  B0,
  output Y
);

  wire and_1_out, and_2_out, and_3_out, and_4_out, not_1_out, not_2_out, not_3_out, not_4_out;

  not not_1 (not_1_out, A1);
  and and_1 (and_1_out, not_1_out, not_2_out);
  not not_2 (not_2_out, B1);
  not not_3 (not_3_out, A0);
  and and_2 (and_2_out, not_3_out, not_4_out);
  not not_4 (not_4_out, B0);
  and and_3 (and_3_out, A0, B0);
  and and_4 (and_4_out, A1, B1);
  or or_1 (Y, and_1_out, and_2_out, and_3_out, and_4_out);
endmodule
