// Logisim project lab12partC-jlh238.circ as structural Verilog: 3 circuits, main circuit main
module main (
  input  Input,
  output Output
);

  wire clock_1_out;
  wire [1:0] Next_State_newstate_0, Register_q;

  Clock clock_1 (.out(clock_1_out));
  Register #(.width(2)) Register (.D(Next_State_newstate_0), .Q(Register_q), .clk(clock_1_out));  // open: en, clr
  Next_State_Func Next_State (
    .State_1(Register_q[1]), .State_0(Register_q[0]), .Input(Input), .NewState_1(Next_State_newstate_0[1]),
    .NewState_0(Next_State_newstate_0[0]));
  Output Output_File (.State_1(Register_q[1]), .State_0(Register_q[0]), .Output_0(Output));
endmodule

module Next_State_Func (
  input  State_1,
  input  State_0,
  input  Input,
  output NewState_1,
  output NewState_0
);

  wire and_1_out, and_2_out, and_3_out, and_4_out, and_5_out, not_1_out, not_2_out, not_3_out, not_4_out,
       not_5_out, not_6_out, not_7_out, not_8_out;

  not not_1 (not_1_out, State_1);
  not not_2 (not_2_out, Input);
  not not_3 (not_3_out, State_0);
  not not_4 (not_4_out, State_1);
  not not_5 (not_5_out, State_0);
  not not_6 (not_6_out, Input);
  not not_7 (not_7_out, State_0);
  not not_8 (not_8_out, Input);
  and and_1 (and_1_out, not_1_out, State_0, not_2_out);
  and and_2 (and_2_out, State_1, not_3_out);
  and and_3 (and_3_out, not_4_out, not_5_out, not_6_out);
  and and_4 (and_4_out, State_1, not_7_out, Input);
  and and_5 (and_5_out, State_1, State_0, not_8_out);
  or or_1 (NewState_1, and_1_out, and_2_out);
  or or_2 (NewState_0, and_3_out, and_4_out, and_5_out);
endmodule

module Output (
  input  State_1,
  input  State_0,
  output Output_0
);

  and and_1 (Output_0, State_1, State_0);
endmodule
